# Fritzing sketch IoTBox_Perfboard (saved by Fritzing 0.9.3b)
perfboards: 1

parts:
  LCD = Header 4 [package=jst-4-pth]
  Buzzer = Header 4 [package=jst-4-pth]
  Switch = Header 4 [package=jst-4-pth]
  Part1 = Photon
  IC1 = MCP23017 I2C I/O Expander  # not connected
  J15 = Camdenboss CTB0158-2 [part_number=CTB0158-2 package=THT]  # not connected

nets:
  N1: LCD.1, Part1.D1
  N2: LCD.2, Buzzer.1, Switch.1, Part1.D0
  N3: LCD.4, Part1.GND
  N4: Buzzer.2, Switch.2
  N5: Buzzer.3, Switch.3, Part1.RST
  N6: Buzzer.4, Switch.4, Part1.D7

custom parts:
  MCP23017 I2C I/O Expander: The MCP23017 uses two i2c pins (these can be shared with other i2c devices), and in exchange gives you 16 general purpose pins. You can set each of 16 pins to be input, output, input with a pullup or open drain. There's even the ability to get an interrupt via an external pin when any of the inputs change so you don't have to keep polling the chip.
